# Fritzing sketch MotionSensor (saved by Fritzing 0.8.3b)
breadboards: 1

parts:
  Part1 = Arduino Uno (Rev3)
  LED1 = RGB LED (com. anode, rbg) [package="5 mm [THT]"]
  R1 = Resistor [tolerance=±5% resistance=220 package=THT]
  R2 = Resistor [tolerance=±5% resistance=220 package=THT]
  PIR1 = PIR sensor

nets:
  GND: Part1.GND, LED1.common_anode, PIR1.GND
  N1: Part1.D9_PWM, R1.Pin_1
  N2: Part1.D10_PWM/SS, R2.Pin_1
  N3: Part1.D2, PIR1.SIG
  5V: Part1.5V, PIR1.VDD
  N4: LED1.red_cathode, R1.Pin_0
  N5: LED1.green_cathode, R2.Pin_0
